# Fritzing sketch diagrama de conexion (saved by Fritzing 0.9.3b)
breadboards: 1

parts:
  Componente1 = Arduino Uno (Rev3)
  IC1 = L293D [package=THT]
  M1 = DC Motor
  M2 = DC Motor
  VCC1 = Battery block 9V
  Componente2 = Bluetooth HC-05 Macho

nets:
  N1: Componente1.D9_PWM, IC1.In_2
  N2: Componente1.D10_PWM/SS, IC1.In_1
  N3: Componente1.D0/RX, Componente2.TXD
  N4: Componente1.D1/TX, Componente2.RXD
  N5: Componente1.D5_PWM, IC1.In_3
  N6: Componente1.D6_PWM, IC1.In_4
  N7: Componente1.5V, IC1.Enable_1
  GND: Componente1.GND, IC1.0V, VCC1.-, Componente2.GND
  N8: IC1.Out_1_(_Controlled_by_Enable_1_), M2.pin_2
  N9: IC1.Out_2_(_Controlled_by_Enable_1_), M2.pin_1
  N10: IC1.Enable_2, IC1.+V, Componente2.VCC
  N11: IC1.Out_3_(_Controlled_by_Enable_2_), M1.pin_2
  N12: IC1.Out_4_(_Controlled_by_Enable_2_), M1.pin_1
